# Fritzing sketch Control_Client (saved by Fritzing 0.9.3b)
breadboards: 1

parts:
  Part1 = Adafruit Feather HUZZAH ESP8266 [part_number="Adafruit #2821"]
  R1 = TRIMPOT [package=3362u-2]
  S1 = Pushbutton [package="[THT]"]
  S2 = Pushbutton [package="[THT]"]
  S3 = Pushbutton [package="[THT]"]
  R2 = Resistor [tolerance=±5% resistance=220 package=THT]
  R3 = Resistor [tolerance=±5% resistance=220 package=THT]
  R4 = Resistor [tolerance=±5% resistance=220 package=THT]
  R5 = Resistor [tolerance=±5% resistance=220 package=THT]  # not connected
  R6 = Resistor [tolerance=±5% resistance=220 package=THT]
  R7 = Resistor [tolerance=±5% resistance=220 package=THT]

nets:
  N1: Part1.GPIO12/MISO, S2.Pin_1, S2.Pin_2, R7.Pin_1
  N2: Part1.GPIO13/MOSI, S3.Pin_1, S3.Pin_2, R6.Pin_1
  N3: Part1.ADC, R1.WIPER
  N4: Part1.GND, R1.CW, R6.Pin_0, R7.Pin_0
  N5: Part1.3.3V, S2.Pin_3, S2.Pin_4, S3.Pin_3, S3.Pin_4, R2.Pin_0
  N6: R1.CCW, R4.Pin_1
  N7: S1.Pin_1, S1.Pin_2
  N8: S1.Pin_3, S1.Pin_4
  N9: R2.Pin_1, R3.Pin_0
  N10: R3.Pin_1, R4.Pin_0

custom parts:
  Adafruit Feather HUZZAH ESP8266: his is the Adafruit Feather HUZZAH ESP8266 - our take on an 'all-in-one' ESP8266 WiFi development board with built in USB and battery charging. Its an ESP8266 WiFi module with all the extras you need, ready to rock! We have other boards in the Feather family, check'em out here. At the Feather HUZZAH's heart is an ESP8266 WiFi microcontroller clocked at 80 MHz and at 3.3V logic. This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
