# Fritzing sketch esp8266_dht22_thinkspeak (saved by Fritzing 0.9.3b)
breadboards: 1

parts:
  Part2 = Adafruit Feather HUZZAH ESP8266 [part_number="Adafruit #2821"]
  LED1 = LED - 5mm [color="Red (635nm)" package="5 mm [THT]"]
  LED2 = LED - 5mm [color="Green (555nm)" package="5 mm [THT]"]
  R1 = Resistor [tolerance=±5% resistance=560 package=THT]
  R2 = Resistor [tolerance=±5% resistance=560 package=THT]
  RHT1 = Humidity and Temperature Sensor RHT03
  R3 = Resistor [tolerance=±5% resistance=10k package=THT]

nets:
  N1: Part2.GPIO12/MISO, RHT1.Data-signal, R3.Pin_0
  N2: Part2.GPIO13/MOSI, R1.Pin_1
  N3: Part2.GPIO14/SCK, R2.Pin_1
  N4: Part2.GND, LED1.cathode, LED2.cathode, RHT1.GND_2
  3.3V: Part2.3.3V, RHT1.Vcc, R3.Pin_1
  N5: LED1.anode, R2.Pin_0
  N6: LED2.anode, R1.Pin_0

custom parts:
  Adafruit Feather HUZZAH ESP8266: his is the Adafruit Feather HUZZAH ESP8266 - our take on an 'all-in-one' ESP8266 WiFi development board with built in USB and battery charging. Its an ESP8266 WiFi module with all the extras you need, ready to rock! We have other boards in the Feather family, check'em out here. At the Feather HUZZAH's heart is an ESP8266 WiFi microcontroller clocked at 80 MHz and at 3.3V logic. This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
