# Fritzing sketch simple-servo-motor (saved by Fritzing 0.9.3b)
breadboards: 1

parts:
  Composant1 = Adafruit Feather HUZZAH ESP8266 [part_number="Adafruit #2821"]
  Servo1 = Basic Servo

nets:
  N1: Composant1.GPIO14/SCK, Servo1.pulse
  GND: Composant1.GND, Servo1.gnd
  3.3V: Composant1.3.3V, Servo1.vcc

custom parts:
  Adafruit Feather HUZZAH ESP8266: his is the Adafruit Feather HUZZAH ESP8266 - our take on an 'all-in-one' ESP8266 WiFi development board with built in USB and battery charging. Its an ESP8266 WiFi module with all the extras you need, ready to rock! We have other boards in the Feather family, check'em out here. At the Feather HUZZAH's heart is an ESP8266 WiFi microcontroller clocked at 80 MHz and at 3.3V logic. This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
